# Fritzing sketch sketch (saved by Fritzing 0.9.3b)
circuit board: 8.46667cm x 5.64444cm
breadboards: 1

parts:
  Q1 = Basic FET N-Channel [part_number=FQP30N06L package="TO220 [THT]"]
  R2 = Resistor [tolerance=±5% resistance=3.9k package=THT]
  U1 = ATTINY45 [package=dip]
  Part2 = FTDI Basic Programmer
  R3 = Resistor [tolerance=±5% resistance=10k package=THT]
  R4 = CdS PHOTOCONDUCTIVE CELL [part_number=GL5528 package=THT]

nets (from the schematic view):
  N1: Q1.gate, R2.Pin_1, R4.pin_0
  N2: Q1.drain, U1.PB5(NRES), R3.Pin_0
  N3: Q1.source, Part2.GND
  N4: R2.Pin_0, U1.GND
  N5: U1.PB0(MOSI), Part2.RXI
  N6: U1.VCC, R4.pin_1
